# Fritzing sketch led-controller-esp32 (saved by Fritzing 0.9.3b)

parts:
  LED1 = LED - 5mm [color="Red (633nm)" package="5 mm [THT]"]
  LED2 = LED - 5mm [color="Yellow (592nm)" package="5 mm [THT]"]
  LED3 = LED - 5mm [color="Blue (470nm)" package="5 mm [THT]"]
  R1 = Resistor [tolerance=±5% resistance=220 package=THT]
  R2 = Resistor [tolerance=±5% resistance=220 package=THT]
  R3 = Resistor [tolerance=±5% resistance=220 package=THT]
  R4 = Resistor [tolerance=±5% resistance=1k package=THT]
  R5 = Photocell (LDR) [package=THT]
  MH-ET_LIVE_ESP32_DEVKIT1 = MH-ET LIVE ESP32 DEVKIT 38 pins

nets:
  N1: LED1.cathode, R1.Pin_0
  N2: LED1.anode, MH-ET_LIVE_ESP32_DEVKIT1.IO5
  N3: LED2.cathode, R2.Pin_0
  N4: LED2.anode, MH-ET_LIVE_ESP32_DEVKIT1.IO18
  N5: LED3.cathode, R3.Pin_0
  N6: LED3.anode, MH-ET_LIVE_ESP32_DEVKIT1.IO19
  N7: R1.Pin_1, R2.Pin_1, R3.Pin_1, R4.Pin_1, MH-ET_LIVE_ESP32_DEVKIT1.GND
  N8: R5.pin_0, MH-ET_LIVE_ESP32_DEVKIT1.3V3
  N9: R5.pin_1, MH-ET_LIVE_ESP32_DEVKIT1.IO34

custom parts:
  MH-ET LIVE ESP32 DEVKIT 38 pins: http://mh.nodebb.com/topic/2/mh-et-live-esp32-devkit
